# Fritzing sketch OLED_WITH_4844_schematic_atmega328 (saved by Fritzing 0.9.3b)
breadboards: 1

parts:
  part = OLED Monochrome 128x64 0.96 inch [part_number=.]
  R3 = Resistor [tolerance=±5% resistance=10k package="0805 [SMD]"]
  R5 = Resistor [tolerance=±5% resistance=10k package="0805 [SMD]"]
  S2 = SWITCH-MOMENTARY-2 [package=tactile-pth]
  S3 = SWITCH-MOMENTARY-2 [package=tactile-pth]
  S1 = SWITCH-MOMENTARY-2 [package=tactile-pth]
  R4 = Resistor [tolerance=±5% resistance=10k package="0805 [SMD]"]
  part_2 = Arduino Pro Mini v13
  R6 = Resistor [tolerance=±5% resistance=10k package="0805 [SMD]"]
  S4 = SWITCH-MOMENTARY-2 [package=tactile-pth]
  SI4844 = IC, DIP package, 24 pins [chip_label=IC]
  R7 = Resistor [tolerance=±5% resistance=10k package=THT]
  R8 = Resistor [tolerance=±5% resistance=10k package=THT]

nets:
  N1: part.SCLK_SCK, part_2.A5, SI4844.pin17, R8.Pin_0
  N2: part.DC_SA0, part_2.A4, SI4844.pin16, R7.Pin_0
  5V: part.VIN, S2.1, S3.1, S1.1, part_2.VCC, S4.1
  GND: part.GND, R3.Pin_1, R5.Pin_0, R4.Pin_0, part_2.GND, R6.Pin_0
  N3: R3.Pin_0, S1.2, part_2.D5_PWM
  N4: R5.Pin_1, S3.2, part_2.D8
  N5: S2.2, R4.Pin_1, part_2.D7
  N6: part_2.D12/MISO, SI4844.pin15
  N7: part_2.D6_PWM, R6.Pin_1, S4.2
  SI48844 P2: part_2.D2
  Arduino: SI4844.pin2
  3.3V: R7.Pin_1, R8.Pin_1

notes:
  Band
  Step
  VFO/BFO
  OLED
  OLED, SI4844, Buttons and Arduino connection.
  Ricardo Lima Caratti - Oct, 2019
  SLC
  SDA
  D8
  D7
  D6
  D5
  Arduino D2 (Interrupt)
  SI4844 Pin 2 (Interrupt)
  RESET (RST)
  BAND UP
  BAND DOWN
  VOLUME UP
  VOLUME DOWN

custom parts:
  OLED Monochrome 128x64 0.96 inch: These displays are small, only about 1" diameter, but very readable due to the high contrast of an OLED display. This display is made of 128x64 individual white OLED pixels, each one is turned on or off by the controller chip. Because the display makes its own light, no backlight is required. This reduces the power required to run the OLED and is why the display has such high contrast; we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
